# Fritzing sketch Sensor Circuit (saved by Fritzing 1.0.1rc)
stripboards: 1

parts:
  S2 = Hall Sensor [part_number=WSH130 package=TO92]
  C3 = Capacitor [package=cap-pth-small2]
  C4 = Capacitor [package=cap-pth-5mm]
  R3 = Resistor [tolerance=±5% power=0.25W resistance=10k package=THT]
  U1 = ESP32-38PinWide [part_number=ESP32-38PinWide]

nets (from the schematic view):
  N1: S2.VCC, C3.1, R3.Pin_0, U1.GPIO14
  N2: S2.GND, C3.2
  N3: S2.OUT, C4.2, R3.Pin_1, U1.VIN
  N4: C4.1, U1.GPIO11

custom parts:
  Hall Sensor: A Hall Sensor
  ESP32-38PinWide: Generic 38-Pin ESP32 with wide format (only access to one side of pins on a breadboard) based on Stephen Lilley's HiLetgo ESP-WROOM-32 ESP32 ESP-32S Development Board.
